# Fritzing sketch board (saved by Fritzing 0.8.7b)
circuit board: 10.6266cm x 5.33905cm
breadboards: 1
perfboards: 1

parts:
  U1 = ATTINY45 [package=dip]
  Pot1 = Dial Potentiometer with switch
  S1 = Pushbutton [package="[THT]"]
  SPKR1 = Loudspeaker
  IC2 = 74LS164N [chip_label=74LS164N package="DIP (Dual Inline) [THT]"]
  D1 = Diode [package=diode-1n4001]
  R1 = Resistor [tolerance=±5% resistance=47k package=THT]
  Q1 = PNP-Transistor [package="TO92 [THT]"]
  R4 = Resistor [tolerance=±5% resistance=25k package=THT]
  IC1 = 74LS138 [chip_label=74LS138 package="DIP (Dual Inline) [THT]"]
  R2 = Resistor [tolerance=±5% resistance=47k package=THT]
  Q2 = PNP-Transistor [package="TO92 [THT]"]
  R3 = Resistor [tolerance=±5% resistance=47k package=THT]
  Q3 = PNP-Transistor [package="TO92 [THT]"]
  D2 = Diode [package=diode-1n4001]
  R5 = Resistor [tolerance=±5% resistance=25k package=THT]
  S2 = Pushbutton [package="[THT]"]
  D3 = Diode [package=diode-1n4001]
  R6 = Resistor [tolerance=±5% resistance=25k package=THT]
  S3 = Pushbutton [package="[THT]"]
  Q4 = NPN-Transistor [package="TO92 [THT]"]
  LED1 = 7-SEGMENT-3DIGIT-PARALIGHT [package=7-segment-3digit-paralight]
  R7 = Resistor [tolerance=±5% resistance=100 package=THT]
  R8 = Resistor [tolerance=±5% resistance=100 package=THT]
  R9 = Resistor [tolerance=±5% resistance=100 package=THT]
  R10 = Resistor [tolerance=±5% resistance=100 package=THT]
  R11 = Resistor [tolerance=±5% resistance=100 package=THT]
  R12 = Resistor [tolerance=±5% resistance=100 package=THT]
  R13 = Resistor [tolerance=±5% resistance=100 package=THT]
  R14 = Resistor [tolerance=±5% resistance=100 package=THT]

nets (from the pcb view):
  N1: U1.PB3(ADC3), IC2.CP
  N2: U1.PB4(ADC2), Q4.B
  N3: U1.PB0(MOSI), IC1.A0
  N4: U1.PB1(MISO), IC1.A1
  N5: U1.PB2(SCK_ADC1), IC2.DSA, IC2.DSB
  N6: Pot1.wiper, Q4.C
  N7: Pot1.leg2, Pot1.switch_leg2
  N8: S1.Pin_1, S1.Pin_2, R4.Pin_1
  N9: S1.Pin_3, S1.Pin_4, D1.A
  N10: SPKR1.pin2, Q4.E
  N11: IC2.Q0, R7.Pin_0
  N12: IC2.Q1, R8.Pin_0
  N13: IC2.Q2, R9.Pin_0
  N14: IC2.Q3, R10.Pin_0
  N15: IC2.Q4, R11.Pin_0
  N16: IC2.Q5, R12.Pin_0
  N17: IC2.Q6, R13.Pin_0
  N18: IC2.Q7, R14.Pin_0
  N19: D1.C, R1.Pin_0, Q1.B, IC1./O0
  N20: R1.Pin_1, Q1.E
  N21: Q1.C, LED1.DIG1
  N22: IC1./O2, R3.Pin_0, Q3.B, D3.C
  N23: IC1./O1, R2.Pin_0, Q2.B, D2.C
  N24: R2.Pin_1, Q2.E
  N25: Q2.C, LED1.DIG2
  N26: R3.Pin_1, Q3.E
  N27: Q3.C, LED1.DP, LED1.C, LED1.DIG3, R9.Pin_1, R14.Pin_1
  N28: D2.A, S2.Pin_3, S2.Pin_4
  N29: R5.Pin_1, S2.Pin_1, S2.Pin_2
  N30: D3.A, S3.Pin_1, S3.Pin_2
  N31: R6.Pin_1, S3.Pin_3
  N32: LED1.E, R11.Pin_1
  N33: LED1.D, R10.Pin_1
  N34: LED1.G, R13.Pin_1
  N35: LED1.F, R12.Pin_1
  N36: LED1.A, R7.Pin_1

custom parts:
  74LS164N: 8-bit serial-in, parallel-out shift register
  74LS138: DIP-16 1 to 8 multiplexer
  NPN-Transistor: A standard NPN-transistor
  7-SEGMENT-3DIGIT-PARALIGHT: A-563G-11 : 3 digits 7 segment display
