# Fritzing sketch board2 (saved by Fritzing 0.8.7b)
circuit board: 9.5cm x 3.8cm
circuit board: 9.58425cm x 5.09176cm
breadboards: 1
perfboards: 1

parts:
  U1 = ATTINY45 [package=dip]
  S1 = Pushbutton [package="[THT]"]
  SPKR1 = Loudspeaker
  IC2 = 74LS164N [chip_label=74LS164N package="DIP (Dual Inline) [THT]"]
  D1 = Diode [package=diode-1n4001]
  R1 = Resistor [tolerance=±5% resistance=47k package=THT]
  Q1 = PNP-Transistor [package="TO92 [THT]"]
  R4 = Resistor [tolerance=±5% resistance=25k package=THT]
  IC1 = 74LS138 [chip_label=74LS138 package="DIP (Dual Inline) [THT]"]
  R2 = Resistor [tolerance=±5% resistance=47k package=THT]
  Q2 = PNP-Transistor [package="TO92 [THT]"]
  R3 = Resistor [tolerance=±5% resistance=47k package=THT]
  Q3 = PNP-Transistor [package="TO92 [THT]"]
  D2 = Diode [package=diode-1n4001]
  S2 = Pushbutton [package="[THT]"]
  D3 = Diode [package=diode-1n4001]
  S3 = Pushbutton [package="[THT]"]
  Q4 = NPN-Transistor [package="TO92 [THT]"]
  LED1 = 7-SEGMENT-3DIGIT-PARALIGHT [package=7-segment-3digit-paralight]
  R7 = Resistor [tolerance=±5% resistance=100 package=THT]
  R8 = Resistor [tolerance=±5% resistance=100 package=THT]
  R9 = Resistor [tolerance=±5% resistance=100 package=THT]
  R10 = Resistor [tolerance=±5% resistance=100 package=THT]
  R11 = Resistor [tolerance=±5% resistance=100 package=THT]
  R12 = Resistor [tolerance=±5% resistance=100 package=THT]
  R13 = Resistor [tolerance=±5% resistance=100 package=THT]
  R14 = Resistor [tolerance=±5% resistance=100 package=THT]
  R15 = Resistor [tolerance=±5% resistance=500 package=THT]
  R16 = Resistor [tolerance=±5% resistance=500 package=THT]
  R17 = Resistor [tolerance=±5% resistance=500 package=THT]
  R18 = Rotary Potentiometer (Small) [maximum_resistance=100kΩ package=THT]
  JP1 = Header 1 [package=1x01_offset]
  JP2 = Header 1 [package=1x01_offset]
  JP3 = Header 1 [package=1x01_offset]
  JP4 = Header 1 [package=1x01_offset]
  JP5 = Header 1 [package=1x01_offset]
  JP6 = Header 1 [package=1x01_offset]
  JP7 = Header 1 [package=1x01_offset]
  JP8 = Header 1 [package=1x01_offset]
  JP9 = Header 1 [package=1x01_offset]
  JP10 = Header 1 [package=1x01_offset]
  JP11 = Header 1 [package=1x01_offset]
  JP12 = Header 1 [package=1x01_offset]
  JP13 = Header 1 [package=1x01_offset]
  JP14 = Header 1 [package=1x01_offset]
  JP15 = Header 1 [package=1x01_offset]
  JP16 = Header 1 [package=1x01_offset]
  JP17 = Header 1 [package=1x01_offset]
  JP18 = Header 1 [package=1x01_offset]
  JP19 = Header 1 [package=1x01_offset]
  JP20 = Header 1 [package=1x01_offset]
  JP21 = Header 1 [package=1x01_offset]
  JP22 = Header 1 [package=1x01_offset]
  BAT1 = Battery Holders [package=battery-aa-kit]
  BAT2 = Battery Holders [package=battery-aa-kit]
  BAT3 = Battery Holders [package=battery-aa-kit]

nets:
  GND: U1.PB5(NRES), U1.GND, IC2.GND, IC2./MR, IC1./E1, IC1./E2, IC1.GND, R18.leg2, BAT1.-
  N1: U1.PB3(ADC3), IC2.CP
  N2: U1.PB4(ADC2), Q4.B
  N3: U1.PB0(MOSI), IC1.A0
  N4: U1.PB1(MISO), IC1.A1
  N5: U1.PB2(SCK_ADC1), IC2.DSA, IC2.DSB
  5V: U1.VCC, SPKR1.pin1, IC2.Vcc, R4.Pin_0, IC1.A2, IC1.E3, IC1.Vcc, BAT2.+
  N6: S1.Pin_1, D1.A
  N7: S1.Pin_3, R4.Pin_1, S2.Pin_3, S2.Pin_4, S3.Pin_3, S3.Pin_4
  N8: SPKR1.pin2, Q4.E
  N9: IC2.Q0, JP19.1
  N10: IC2.Q1, JP17.1
  N11: IC2.Q2, JP16.1
  N12: IC2.Q3, JP18.1
  N13: IC2.Q4, JP2.1
  N14: IC2.Q5, JP5.1
  N15: IC2.Q6, JP4.1
  N16: IC2.Q7, JP3.1
  N17: D1.C, IC1./O0, JP20.1
  N18: R1.Pin_0, Q1.B, R15.Pin_1
  N19: R1.Pin_1, Q1.E, R2.Pin_1, Q2.E, R3.Pin_1, Q3.E
  N20: Q1.C, LED1.DIG1
  N21: IC1./O2, D3.C, JP21.1
  N22: IC1./O1, D2.C, JP22.1
  N23: R2.Pin_0, Q2.B, R16.Pin_1
  N24: Q2.C, LED1.DIG2
  N25: R3.Pin_0, Q3.B, R17.Pin_1
  N26: Q3.C, LED1.DP, LED1.DIG3, R14.Pin_1
  N27: D2.A, S2.Pin_1, S2.Pin_2
  N28: D3.A, S3.Pin_1, S3.Pin_2
  N29: Q4.C, R18.wiper
  N30: LED1.E, R11.Pin_1
  N31: LED1.D, R10.Pin_1
  N32: LED1.C, R9.Pin_1
  N33: LED1.G, R13.Pin_1
  N34: LED1.B, R8.Pin_1
  N35: LED1.F, R12.Pin_1
  N36: LED1.A, R7.Pin_1
  N37: R7.Pin_0, JP12.1
  N38: R8.Pin_0, JP7.1
  N39: R9.Pin_0, JP9.1
  N40: R10.Pin_0, JP11.1
  N41: R11.Pin_0, JP1.1
  N42: R12.Pin_0, JP6.1
  N43: R13.Pin_0, JP8.1
  N44: R14.Pin_0, JP10.1
  N45: R15.Pin_0, JP15.1
  N46: R16.Pin_0, JP14.1
  N47: R17.Pin_0, JP13.1
  N48: BAT1.+, BAT3.-
  N49: BAT2.-, BAT3.+

custom parts:
  74LS164N: 8-bit serial-in, parallel-out shift register
  74LS138: DIP-16 1 to 8 multiplexer
  NPN-Transistor: A standard NPN-transistor
  7-SEGMENT-3DIGIT-PARALIGHT: A-563G-11 : 3 digits 7 segment display
